# Fritzing sketch CirclingCar-reduced (saved by Fritzing 0.9.2b)
breadboards: 1

parts:
  Part1 = Arduino Nano (Rev3.0)
  J1 = Basic Servo  # not connected
  J2 = Basic Servo  # not connected
  Power_plug1 = Power plug
  IR1 = TSOP312.., 314.. [package=THT]  # not connected
  IR2 = TSOP312.., 314.. [package=THT]  # not connected
  S2 = Square Pushbutton
  S3 = Square Pushbutton

nets:
  GND: Part1.GND, Power_plug1.GND, S2.leg0, S3.leg1
  N1: Part1.D2, S2.leg1
  N2: Part1.D3, S3.leg0
  VIN: Part1.VIN, Power_plug1.VCC
