# Fritzing sketch CirclingCar (saved by Fritzing 0.9.2b)
breadboards: 1

parts:
  Part1 = Arduino Nano (Rev3.0)
  J1 = Basic Servo
  J2 = Basic Servo
  Power_plug1 = Power plug
  IR1 = TSOP312.., 314.. [package=THT]
  IR2 = TSOP312.., 314.. [package=THT]
  S2 = Square Pushbutton
  S3 = Square Pushbutton

nets:
  GND: Part1.GND, J1.gnd, J2.gnd, Power_plug1.GND, IR1.GND, IR2.GND, S2.leg0, S3.leg1
  N1: Part1.D2, S2.leg1
  N2: Part1.D3, S3.leg0
  N3: Part1.D9, J1.pulse
  N4: Part1.D10, J2.pulse
  N5: Part1.D11/MOSI, IR1.Data
  N6: Part1.D12/MISO, IR2.Data
  VIN: Part1.VIN, Power_plug1.VCC
  VCC: Part1.5V, J1.vcc, J2.vcc, IR1.Vs, IR2.Vs
